# Fritzing sketch Uno-esp8266 (saved by Fritzing 0.9.5d)
breadboards: 1

parts:
  Part1 = Arduino Uno (Rev3) - ICSP
  Espessif_Serial_Wifi_Modul_1 = ESP8266 ESP01 [part_number=ESP8266 package=THT]

nets:
  N1: Part1.D2, Espessif_Serial_Wifi_Modul_1.TXD
  N2: Part1.D3_PWM, Espessif_Serial_Wifi_Modul_1.RXD
  3V3: Part1.3V3, Espessif_Serial_Wifi_Modul_1.VCC
  GND: Part1.GND, Espessif_Serial_Wifi_Modul_1.GND

custom parts:
  ESP8266 ESP01: Generic WiFi Module based on the ESP8266 with onboard PCB antenna and UART communications
